# Fritzing sketch collegamenti (saved by Fritzing 0.9.1b)

parts:
  Arduino_Yun = Arduino Yun

nets:
  PH Meter: Arduino_Yun.A0
  EC1 B: Arduino_Yun.A1
  EC2 B: Arduino_Yun.A2
  Pump 1: Arduino_Yun.ICSP_MISO, Arduino_Yun.D12/MISO
  Pump 2: Arduino_Yun.ICSP_SCK, Arduino_Yun.D13/SCK
  GND: Arduino_Yun.GND
  Lamp 2: Arduino_Yun.D8
  Fertilizzante: Arduino_Yun.D2
  EC1 A: Arduino_Yun.D3_PWM
  EC1 C: Arduino_Yun.D4
  EC2 A: Arduino_Yun.D5_PWM
  EC2 C: Arduino_Yun.D6_PWM
  Lamp 1: Arduino_Yun.D7
  5V: Arduino_Yun.5V
